# Fritzing sketch Servo + Lichtmessung (saved by Fritzing 0.8.7b)
breadboards: 1

parts:
  R1 = PHOTOCELL [package=photocell-kit]
  J1 = Basic Servo
  Bauteil1 = Arduino Uno (Rev3)
  R2 = Resistor [tolerance=±5% resistance=220 package="0805 [SMD]"]

nets:
  N1: R1.P$1, Bauteil1.D0/RX, R2.Pin_1
  VCC: R1.P$2, J1.vcc, Bauteil1.5V
  GND: J1.gnd, Bauteil1.GND, R2.Pin_0
  N2: J1.pulse, Bauteil1.D8
